# Fritzing sketch IoT (saved by Fritzing 0.9.3b)
breadboards: 1

parts:
  Componente1 = Arduino Uno (Rev3)
  RHT1 = Humidity and Temperature Sensor RHT03
  IC1 = DS1302 [package="SO8 [SMD]"]
  U1 = 7-SEGMENT-4DIGIT [package=7-segment-4digit]
  GSM_SIM_GPSR_SMS_SIM900_SIM1 = SIM800L [package=THT]

nets:
  N1: Componente1.A4/SDA, IC1.I/O_-_SPI_Data_In/Out
  N2: Componente1.A5/SCL, IC1.SCLK_-_SPI_Clock
  N3: Componente1.D8, U1.5
  N4: Componente1.D9_PWM, U1.3, U1.4
  N5: Componente1.D5_PWM, RHT1.Data-signal
  5V: Componente1.5V, RHT1.GND_2, IC1.+V, U1.7, GSM_SIM_GPSR_SMS_SIM900_SIM1.VDD
  GND: Componente1.GND, IC1.0V, U1.6, GSM_SIM_GPSR_SMS_SIM900_SIM1.GND
